# Fritzing sketch NFC_MED_v3 (saved by Fritzing 0.9.3b)

parts:
  Part1 = Arduino Nano (Rev3.0) (ICSP)
  OLED1 = OLED 128x64 I2C Monochrome Display GND-VDD
  SD_card_module1 = SD Card Module
  ZS-042_RTC1 = ZS-042 RTC Module
  Part2 = RFID-RC522-v2
  R1 = Resistor [tolerance=±5% resistance=100k package=THT]

nets:
  N1: Part1.D5, Part2.RST
  N2: Part1.D8, Part2.SDA
  N3: Part1.D10, SD_card_module1.CS
  N4: Part1.D11/MOSI, SD_card_module1.MOSI, Part2.MOSI
  N5: Part1.D12/MISO, Part2.MISO, R1.Pin_0
  GND: Part1.GND, OLED1.GND, SD_card_module1.GND, ZS-042_RTC1.GND, Part2.GND
  5V: Part1.5V, OLED1.VDD, SD_card_module1.+5, ZS-042_RTC1.VCC
  N6: Part1.A5, OLED1.SCK, ZS-042_RTC1.SCL
  N7: Part1.A4, OLED1.SDA, ZS-042_RTC1.SDA
  3V3: Part1.3V3, Part2.3.3V
  N8: Part1.D13/SCK, SD_card_module1.SCK, Part2.SCK
  N9: SD_card_module1.MISO, R1.Pin_1

custom parts:
  OLED 128x64 I2C Monochrome Display GND-VDD: OLED 128x64 I2C Monochrome Display. Note: there are two variants of this part, this one is the GND VDD SCK SDA variant. The other is VDD GND SCK SDA. Make sure you select the part that matches your module as using the incorrect part will probably destroy your module! In addition the mounting holes are marked on silkscreen but not by default drilled. If you want drilled mounting holes, copy a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
  SD Card Module: SD Card Module Slot Socket Reader For Arduino ARM MCU
  RFID-RC522-v2: A simple China made RFID-RC522 Reader; do check the pin labels, as this is a MFRC522 based clone.
